// Logisim project 16bit_processor_T3.circ as structural Verilog: 1 circuit, main circuit main
module main (
  input  [3:0] in_1,
  input  in_2,
  input  [15:0] in_3,
  input  [8:0] in_4,
  input  in_5,
  input  in_6,
  input  [15:0] in_7,
  input  in_8,
  input  in_9,
  input  in_10,
  input  [15:0] in_11,
  input  [15:0] in_12,
  input  [15:0] in_13,
  output [15:0] out_14,
  output [15:0] out_15,
  output [15:0] out_16
);

  wire clock_1_out, clock_2_out, clock_3_out, clock_4_out, comparator_1_lt, decoder_1_out0, decoder_1_out1,
       decoder_1_out2, decoder_1_out3, decoder_1_out4, decoder_1_out5, decoder_1_out6, decoder_1_out7,
       decoder_1_out8, decoder_1_out9, decoder_1_out10, decoder_1_out11, decoder_1_out12, decoder_1_out13,
       decoder_1_out14, decoder_1_out15, decoder_2_out0, decoder_2_out1, decoder_2_out2, decoder_2_out3,
       decoder_2_out4, decoder_2_out5, decoder_2_out6, decoder_2_out7, not_1_out, not_2_out, not_3_out,
       or_1_out, or_2_out, or_3_out, or_4_out;
  wire [3:0] adder_1_out, multiplexer_5_out_2, PC_q, ram_2_data;
  wire [8:0] multiplexer_2_out, ram_2_data_3;
  wire [11:9] ram_2_data_2;
  wire [15:0] adder_2_out, adder_3_out, and_1_out, divider_1_out, multiplexer_1_out, multiplexer_3_out,
       multiplexer_4_out, multiplier_1_out, not_4_out, or_5_out, R0_q, R1_q, R2_q, R3_q, R4_q, R5_q, R6_q,
       R7_q, register_1_q, register_2_q, shifter_1_out, shifter_2_out, shifter_3_out, shifter_4_out,
       subtractor_1_out, subtractor_2_out;
  wire [15:4] multiplexer_5_out;

  Clock clock_1 (.out(clock_1_out));
  Clock clock_2 (.out(clock_2_out));
  Clock clock_3 (.out(clock_3_out));
  Multiplexer #(.width(16), .enable("false")) multiplexer_1 (
    .in0(out_15), .in1(register_1_q), .out(multiplexer_1_out), .sel(decoder_1_out11));
  Decoder #(.select(4), .enable("false")) decoder_1 (
    .out0(decoder_1_out0), .out1(decoder_1_out1), .out2(decoder_1_out2), .out3(decoder_1_out3),
    .out4(decoder_1_out4), .out5(decoder_1_out5), .out6(decoder_1_out6), .out7(decoder_1_out7),
    .out8(decoder_1_out8), .out9(decoder_1_out9), .out10(decoder_1_out10), .out11(decoder_1_out11),
    .out12(decoder_1_out12), .out13(decoder_1_out13), .out14(decoder_1_out14), .out15(decoder_1_out15),
    .sel(ram_2_data));
  Multiplexer #(.width(9), .enable("false")) multiplexer_2 (
    .in0(ram_2_data_3), .in1(in_4), .out(multiplexer_2_out), .sel(in_6));
  Multiplexer #(.width(16), .enable("false")) multiplexer_3 (
    .in0(multiplexer_1_out), .in1(in_7), .out(multiplexer_3_out), .sel(in_8));
  or or_1 (or_1_out, or_2_out, decoder_1_out1);
  or or_2 (or_2_out, in_10, decoder_1_out11);
  or or_3 (or_3_out, decoder_1_out2, decoder_1_out3, decoder_1_out4, decoder_1_out5, decoder_1_out6, decoder_1_out7, decoder_1_out8, decoder_1_out9, decoder_1_out10, decoder_1_out12, decoder_1_out13, decoder_1_out14, decoder_1_out15);
  Adder #(.width(4)) adder_1 (.a(PC_q), .b(in_1), .out(adder_1_out));  // open: cin, cout
  not not_1 (not_1_out, in_5);
  not not_2 (not_2_out, decoder_1_out1);
  RAM #(.addrWidth(9), .dataWidth(16), .bus("separate")) ram_1 (
    .addr(multiplexer_2_out), .din(multiplexer_3_out), .data(out_14), .str(or_1_out), .clk(clock_1_out),
    .ld(not_2_out), .clr(in_9));  // open: sel
  Register #(.width(16)) register_1 (
    .D(out_15), .en(decoder_1_out11), .Q(register_1_q), .clk(clock_2_out));  // open: clr
  or or_4 (or_4_out, decoder_1_out0, decoder_1_out11);
  Register #(.width(4)) PC (.D(adder_1_out), .en(in_5), .Q(PC_q), .clk(clock_3_out), .clr(in_2));
  Multiplexer #(.width(16), .enable("false")) multiplexer_4 (
    .in0(register_2_q), .in1(out_14), .out(multiplexer_4_out), .sel(or_4_out));
  Comparator #(.width(16)) comparator_1 (.a(out_14), .b(in_13), .lt(comparator_1_lt));  // open: gt, eq
  RAM #(.addrWidth(4), .dataWidth(16), .bus("separate")) ram_2 (
    .addr(PC_q), .din(in_3), .data({ram_2_data, ram_2_data_2, ram_2_data_3}), .str(not_1_out),
    .clk(clock_3_out), .ld(in_5));  // open: sel, clr
  Register #(.width(16)) R0 (.D(multiplexer_4_out), .en(decoder_2_out0), .Q(R0_q), .clk(clock_4_out));  // open: clr
  Register #(.width(16)) R1 (.D(multiplexer_4_out), .en(decoder_2_out1), .Q(R1_q), .clk(clock_4_out));  // open: clr
  Register #(.width(16)) R2 (.D(multiplexer_4_out), .en(decoder_2_out2), .Q(R2_q), .clk(clock_4_out));  // open: clr
  Register #(.width(16)) R3 (.D(multiplexer_4_out), .en(decoder_2_out3), .Q(R3_q), .clk(clock_4_out));  // open: clr
  Register #(.width(16)) R4 (.D(multiplexer_4_out), .en(decoder_2_out4), .Q(R4_q), .clk(clock_4_out));  // open: clr
  Register #(.width(16)) R5 (.D(multiplexer_4_out), .en(decoder_2_out5), .Q(R5_q), .clk(clock_4_out));  // open: clr
  Register #(.width(16)) R6 (.D(multiplexer_4_out), .en(decoder_2_out6), .Q(R6_q), .clk(clock_4_out));  // open: clr
  Register #(.width(16)) R7 (.D(multiplexer_4_out), .en(decoder_2_out7), .Q(R7_q), .clk(clock_4_out));  // open: clr
  Clock clock_4 (.out(clock_4_out));
  Decoder #(.select(3), .enable("false")) decoder_2 (
    .out0(decoder_2_out0), .out1(decoder_2_out1), .out2(decoder_2_out2), .out3(decoder_2_out3),
    .out4(decoder_2_out4), .out5(decoder_2_out5), .out6(decoder_2_out6), .out7(decoder_2_out7),
    .sel(ram_2_data_2));
  Multiplexer #(.width(16), .enable("false")) multiplexer_5 (
    .in0(in_12), .in1(out_14), .out({multiplexer_5_out, multiplexer_5_out_2}), .sel(comparator_1_lt));
  Multiplexer #(.select(3), .width(16)) multiplexer_6 (
    .in0(R0_q), .in1(R1_q), .in2(R2_q), .in3(R3_q), .in4(R4_q), .in5(R5_q), .in6(R6_q), .in7(R7_q),
    .out(out_15), .sel(ram_2_data_2), .en(not_3_out));
  not not_3 (not_3_out, clock_4_out);
  Register #(.width(16)) register_2 (.D(out_16), .en(or_3_out), .Q(register_2_q), .clk(clock_2_out));  // open: clr
  Adder #(.width(16)) adder_2 (.a(out_14), .b(out_15), .out(adder_2_out));  // open: cin, cout
  Subtractor #(.width(16)) subtractor_1 (.a(out_15), .b(out_14), .out(subtractor_1_out));  // open: bin, bout
  Multiplier #(.width(16)) multiplier_1 (.a(out_14), .b(out_15), .out(multiplier_1_out));  // open: cin, cout
  Divider #(.width(16)) divider_1 (.a(out_15), .b(out_14), .out(divider_1_out));  // open: upper, rem
  Adder #(.width(16)) adder_3 (.a(out_15), .b(in_11), .out(adder_3_out));  // open: cin, cout
  Subtractor #(.width(16)) subtractor_2 (.a(out_15), .b(in_11), .out(subtractor_2_out));  // open: bin, bout
  assign and_1_out = out_14 & out_15;  // AND_Gate and_1, 16 bits wide
  assign or_5_out = out_14 | out_15;  // OR_Gate or_5, 16 bits wide
  assign not_4_out = ~out_15;  // NOT_Gate not_4, 16 bits wide
  Shifter #(.width(16), .shift("lr")) shifter_1 (.in(out_15), .\dist (multiplexer_5_out_2), .out(shifter_1_out));
  Shifter #(.width(16)) shifter_2 (.in(out_15), .\dist (multiplexer_5_out_2), .out(shifter_2_out));
  Shifter #(.width(16), .shift("rr")) shifter_3 (.in(out_15), .\dist (multiplexer_5_out_2), .out(shifter_3_out));
  Shifter #(.width(16), .shift("rl")) shifter_4 (.in(out_15), .\dist (multiplexer_5_out_2), .out(shifter_4_out));
  Multiplexer #(.select(4), .width(16), .enable("false")) multiplexer_7 (
    .in2(adder_2_out), .in3(subtractor_1_out), .in4(multiplier_1_out), .in5(divider_1_out),
    .in6(adder_3_out), .in7(subtractor_2_out), .in8(and_1_out), .in9(or_5_out), .in10(not_4_out),
    .in12(shifter_1_out), .in13(shifter_2_out), .in14(shifter_3_out), .in15(shifter_4_out), .out(out_16),
    .sel(ram_2_data));  // open: in0, in1, in11

  // Notes on the sheet:
  //   Main memory
  //   Instruction Memory
  //   Register file
  //   Accumulator
  //   ALU
  //   0010
  //   0100
  //   0110
  //   1000
  //   1001
  //   1010
  //   0011
  //   0101
  //   0111
endmodule
